// Digital circuit bw8.dig as structural Verilog
module bw8 (
  input  Nmi,
  input  Irq,
  input  Req
);

  wire add_carry, and_4_out, and_5_out, AssertSystemBus, carry, clk, EnableExtension, EnterKernelMode,
       JumpDecoder_d, left_shift_carry, left_sign, LoadA, LoadB, LoadBR, LoadC, LoadD, LoadFlags, LoadIR,
       LoadOffset, LoadPC_H, LoadPC_L, LoadSP_H, LoadSP_L, LoadTPtr_H, LoadTPtr_L, LoadTReg, LoadX_H,
       LoadX_L, LoadY_H, LoadY_L, multiplexer_11_out, nCodeAccess, negative, NewIrqEnable, NewnKernel,
       NewNmiActive, NewUserData, nIOAccess, or_1_out, or_2_out, or_4_out, PointerWriteBackSelect,
       RegisterLoadEnable, RegisterWriteBackSelect, ResultSelect, right_shift_carry, Sequencer_ovf,
       SetNmiActive, Write;
  wire [1:0] AdderSelect, CarrySelect, InterruptMode, IrqEnableFlagControl, OffsetMode, or_3_out,
       PointerLoadEnable, priorityencoder_1_num, ShiftSelect, UserDataFlagControl;
  wire [1:1] InterruptLatch_q;
  wire [2:0] Control, JumpCondition, LeftSelect, mcr, multiplexer_3_out_2, PointerLoadSelect, PointerSelect,
       RegisterLoadSelect, RightSelect, seq;
  wire [2:1] NewAluFlags;
  wire [3:0] AluFlags, AluFunction, and_1_out, Bank, br, Flags, LogicSelect, mbr, multiplexer_1_out_2,
       multiplexer_2_out_2, multiplexer_15_out, multiplexer_19_out, multiplexer_20_out;
  wire [4:4] and_2_out, and_3_out;
  wire [6:0] result, shift, SHL_out;
  wire [7:0] areg, ASR_out, breg, creg, DataBus, decoder_1_out_0, decoder_2_out_0, decoder_3_out_0, dreg, ir,
       \logic , mdi, mdo, MemoryData, multiplexer_1_out, multiplexer_2_out, multiplexer_4_out,
       multiplexer_5_out, multiplexer_6_out, multiplexer_12_out, multiplexer_13_out, off, temp;
  wire [7:1] SHR_out;
  wire [10:0] AluDecoder_d;
  wire [11:11] Extension_Bit_q;
  wire [14:14] ControlLines_q;
  wire [15:0] add_2_s, Address, bitextender_1_out, mar, multiplexer_7_out, multiplexer_8_out, pc, sp, tp, xp,
       yp;
  wire [23:0] multiplexer_3_out;
  wire [40:0] InterruptDecoder_d, PrimaryDecoder_d;

  or or_1 (or_1_out, Sequencer_ovf, ControlLines_q[14]);
  Decoder #(.Selector_Bits(3)) decoder_1 (
    .sel(PointerLoadSelect), .out_0(decoder_1_out_0[7]), .out_1(decoder_1_out_0[6]),
    .out_2(decoder_1_out_0[5]), .out_3(decoder_1_out_0[4]), .out_4(decoder_1_out_0[3]),
    .out_5(decoder_1_out_0[2]), .out_6(decoder_1_out_0[1]), .out_7(decoder_1_out_0[0]));
  Decoder #(.Selector_Bits(3)) decoder_2 (
    .sel(PointerLoadSelect), .out_0(decoder_2_out_0[0]), .out_1(decoder_2_out_0[1]),
    .out_2(decoder_2_out_0[2]), .out_3(decoder_2_out_0[3]), .out_4(decoder_2_out_0[4]),
    .out_5(decoder_2_out_0[5]), .out_6(decoder_2_out_0[6]), .out_7(decoder_2_out_0[7]));
  Counter #(.Bits(3)) Sequencer (.en(1'b1), .C(clk), .clr(ControlLines_q[14]), .out(seq), .ovf(Sequencer_ovf));
  Register #(.Bits(8)) Instruction_Register (.D(DataBus), .C(clk), .en(LoadIR), .Q(ir));
  RS_FF Extension_Bit (.S(EnableExtension), .C(clk), .R(or_1_out), .Q(Extension_Bit_q[11]));  // open: nQ
  D_FF #(.Bits(3)) InterruptLatch (
    .D({Nmi, Irq, Req}), .C(clk), .Q({and_1_out[3], InterruptLatch_q[1], and_1_out[0]}));  // open: nQ
  Multiplexer #(.Bits(8)) multiplexer_1 (
    .sel(PointerLoadEnable[1]), .in_0({8{1'b0}}), .in_1(decoder_1_out_0),
    .out({multiplexer_1_out[7:5], multiplexer_1_out_2, multiplexer_1_out[0]}));
  Multiplexer #(.Bits(8)) multiplexer_2 (
    .sel(PointerLoadEnable[0]), .in_0({8{1'b0}}), .in_1(decoder_2_out_0),
    .out({multiplexer_2_out[7:5], multiplexer_2_out_2, multiplexer_2_out[0]}));
  ROM #(.AddrBits(7)) JumpDecoder (.A({AluFlags, JumpCondition}), .sel(1'b1), .D(JumpDecoder_d));
  ROM #(.AddrBits(12), .Bits(41)) PrimaryDecoder (.A({Extension_Bit_q[11], ir, seq}), .sel(1'b1), .D(PrimaryDecoder_d));
  D_FF #(.Bits(2)) u_InterruptMode (.D(priorityencoder_1_num), .C(or_1_out), .Q(InterruptMode));  // open: nQ
  and and_1 (and_1_out[1], Flags[0], InterruptLatch_q[1]);
  // NotConnected on and_1_out[2]
  PriorityEncoder #(.Selector_Bits(2)) priorityencoder_1 (
    .in0(1'b0), .in1(and_1_out[3]), .in2(and_1_out[1]), .in3(and_1_out[0]), .num(priorityencoder_1_num));  // open: any
  and and_2 (and_2_out[4], multiplexer_1_out[0], JumpDecoder_d);
  and and_3 (and_3_out[4], multiplexer_2_out[0], JumpDecoder_d);
  ROM #(.AddrBits(5), .Bits(41)) InterruptDecoder (.A({InterruptMode, seq}), .sel(1'b1), .D(InterruptDecoder_d));
  or or_2 (or_2_out, InterruptMode[0], InterruptMode[1]);
  Multiplexer #(.Bits(41)) multiplexer_3 (
    .sel(or_2_out), .in_0(PrimaryDecoder_d), .in_1(InterruptDecoder_d),
    .out({PointerLoadEnable, PointerLoadSelect, JumpCondition, AluFunction, RegisterLoadSelect, RegisterLoadEnable, or_3_out[1], multiplexer_3_out[23:10], multiplexer_3_out_2, multiplexer_3_out[6:0]}));
  D_FF #(.Bits(5)) PointerControlLines (
    .D({and_2_out[4], multiplexer_1_out_2}), .C(clk), .Q({LoadPC_H, LoadSP_H, LoadX_H, LoadY_H, LoadTPtr_H}));  // open: nQ
  D_FF #(.Bits(5)) PointerControlLines_2 (
    .D({and_3_out[4], multiplexer_2_out_2}), .C(clk), .Q({LoadPC_L, LoadSP_L, LoadX_L, LoadY_L, LoadTPtr_L}));  // open: nQ
  or or_3 (or_3_out[0], multiplexer_3_out_2[2], multiplexer_3_out_2[1], multiplexer_3_out_2[0]);
  Decoder #(.Selector_Bits(3)) decoder_3 (
    .sel(RegisterLoadSelect), .out_0(decoder_3_out_0[0]), .out_1(decoder_3_out_0[1]),
    .out_2(decoder_3_out_0[2]), .out_3(decoder_3_out_0[3]), .out_4(decoder_3_out_0[4]),
    .out_5(decoder_3_out_0[5]), .out_6(decoder_3_out_0[6]), .out_7(decoder_3_out_0[7]));
  Multiplexer #(.Bits(8)) multiplexer_4 (
    .sel(RegisterLoadEnable), .in_0({8{1'b0}}), .in_1(decoder_3_out_0), .out(multiplexer_4_out));
  ROM #(.AddrBits(4), .Bits(11)) AluDecoder (.A(AluFunction), .sel(1'b1), .D(AluDecoder_d));
  // Probe Instruction Register on ir
  // Probe Sequencer on seq
  // Probe InterruptMode on InterruptMode
  D_FF #(.Bits(24)) ControlLines (
    .D({multiplexer_3_out[23:10], multiplexer_3_out_2, multiplexer_3_out[6:0]}), .C(clk),
    .Q({Write, LoadFlags, EnterKernelMode, SetNmiActive, UserDataFlagControl, IrqEnableFlagControl, EnableExtension, ControlLines_q[14], AssertSystemBus, OffsetMode, PointerWriteBackSelect, PointerSelect, RegisterWriteBackSelect, RightSelect, LeftSelect}));  // open: nQ
  D_FF #(.Bits(2)) BusControlLines (.D(or_3_out), .C(clk), .Q({nIOAccess, nCodeAccess}));  // open: nQ
  // Probe on areg
  // Probe on breg
  // Probe on creg
  // Probe on dreg
  // Probe on temp
  // Probe on \logic 
  // Probe on {left_sign, shift}
  // Probe on {negative, result}
  D_FF #(.Bits(8)) RegisterControlLines (
    .D(multiplexer_4_out), .C(clk), .Q({LoadIR, LoadTReg, LoadBR, LoadOffset, LoadD, LoadC, LoadB, LoadA}));  // open: nQ
  D_FF #(.Bits(11)) AluControlLines (
    .D(AluDecoder_d), .C(clk), .Q({ResultSelect, CarrySelect, AdderSelect, LogicSelect, ShiftSelect}));  // open: nQ
  // Probe on pc
  // Probe on sp
  // Probe on xp
  // Probe on yp
  // Probe on tp
  // Probe on mcr
  // Probe on mbr
  // Probe on mar
  // Probe on mdo
  // Probe on mdi
  Register #(.Bits(8)) GPR_A (.D(DataBus), .C(clk), .en(LoadA), .Q(areg));
  Register #(.Bits(8)) GPR_B (.D(DataBus), .C(clk), .en(LoadB), .Q(breg));
  Register #(.Bits(8)) GPR_C (.D(DataBus), .C(clk), .en(LoadC), .Q(creg));
  Register #(.Bits(8)) GPR_D (.D(DataBus), .C(clk), .en(LoadD), .Q(dreg));
  Register #(.Bits(8)) u_Temp (.D(DataBus), .C(clk), .en(LoadTReg), .Q(temp));
  Register #(.Bits(8), .isProgramCounter("true")) register_1 (
    .D(multiplexer_7_out[15:8]), .C(clk), .en(LoadPC_H), .Q(pc[15:8]));
  Register #(.Bits(8), .isProgramCounter("true")) register_2 (
    .D(multiplexer_7_out[15:8]), .C(clk), .en(LoadSP_H), .Q(sp[15:8]));
  Register #(.Bits(8), .isProgramCounter("true")) register_3 (
    .D(multiplexer_7_out[15:8]), .C(clk), .en(LoadX_H), .Q(xp[15:8]));
  Register #(.Bits(8), .isProgramCounter("true")) register_4 (
    .D(multiplexer_7_out[15:8]), .C(clk), .en(LoadY_H), .Q(yp[15:8]));
  Register #(.Bits(8), .isProgramCounter("true")) register_5 (
    .D(multiplexer_7_out[15:8]), .C(clk), .en(LoadTPtr_H), .Q(tp[15:8]));
  Register #(.Bits(8), .isProgramCounter("true")) register_6 (
    .D(multiplexer_7_out[7:0]), .C(clk), .en(LoadPC_L), .Q(pc[7:0]));
  Register #(.Bits(8), .isProgramCounter("true")) register_7 (
    .D(multiplexer_7_out[7:0]), .C(clk), .en(LoadSP_L), .Q(sp[7:0]));
  Register #(.Bits(8), .isProgramCounter("true")) register_8 (
    .D(multiplexer_7_out[7:0]), .C(clk), .en(LoadX_L), .Q(xp[7:0]));
  Register #(.Bits(8), .isProgramCounter("true")) register_9 (
    .D(multiplexer_7_out[7:0]), .C(clk), .en(LoadY_L), .Q(yp[7:0]));
  Register #(.Bits(8), .isProgramCounter("true")) register_10 (
    .D(multiplexer_7_out[7:0]), .C(clk), .en(LoadTPtr_L), .Q(tp[7:0]));
  Multiplexer #(.Selector_Bits(3), .Bits(8)) multiplexer_5 (
    .sel(LeftSelect), .in_0(areg), .in_1(breg), .in_2(creg), .in_3(dreg), .in_4(temp), .in_5({8{1'b0}}),
    .in_6({8{1'b0}}), .in_7({8{1'b0}}), .out(multiplexer_5_out));
  Multiplexer #(.Selector_Bits(3), .Bits(8)) multiplexer_6 (
    .sel(RightSelect), .in_0(areg), .in_1(breg), .in_2(creg), .in_3(dreg), .in_4(temp), .in_5({8{1'b0}}),
    .in_6({8{1'b0}}), .in_7({8{1'b0}}), .out(multiplexer_6_out));
  Multiplexer #(.Bits(16)) multiplexer_7 (
    .sel(PointerWriteBackSelect), .in_0({DataBus, DataBus}), .in_1(add_2_s), .out(multiplexer_7_out));
  Multiplexer #(.Selector_Bits(3), .Bits(16)) multiplexer_8 (
    .sel(PointerSelect), .in_0(pc), .in_1(sp), .in_2(xp), .in_3(yp), .in_4(tp), .in_5(16'h3), .in_6(16'h6),
    .in_7(16'h9), .out(multiplexer_8_out));
  BarrelShifter #(.Bits(8)) SHL (.in(multiplexer_5_out), .shift(4'b0001), .out({left_shift_carry, SHL_out}));
  BarrelShifter #(.Bits(8), .direction("right")) SHR (
    .in(multiplexer_5_out), .shift(4'b0001), .out({SHR_out, right_shift_carry}));
  BarrelShifter #(.Bits(8), .barrelShifterMode("arithmetic"), .direction("right")) ASR (
    .in(multiplexer_5_out), .shift(4'b0001), .out(ASR_out));
  Multiplexer #(.Selector_Bits(2), .Bits(8)) multiplexer_9 (
    .sel(ShiftSelect), .in_0({left_shift_carry, SHL_out}), .in_1({SHR_out, right_shift_carry}),
    .in_2(ASR_out), .in_3(multiplexer_5_out), .out({left_sign, shift}));
  ROM #(.AddrBits(20), .Bits(8)) Logic_Unit (
    .A({LogicSelect, multiplexer_6_out, multiplexer_5_out}), .sel(1'b1), .D(\logic ));
  Multiplexer #(.Selector_Bits(2)) multiplexer_10 (
    .sel(CarrySelect), .in_0(1'b0), .in_1(add_carry), .in_2(right_shift_carry), .in_3(left_shift_carry),
    .out(carry));
  Button button_1 (.out(clk));
  Register #(.Bits(8)) Offset_Register (.D(DataBus), .C(clk), .en(LoadOffset), .Q(off));
  and and_4 (and_4_out, Flags[1], nCodeAccess);
  Add #(.Bits(8)) add_1 (
    .a({left_sign, shift}), .b(\logic ), .c_i(multiplexer_11_out), .s({negative, result}), .c_o(add_carry));
  Comparator #(.Bits(8)) comparator_1 (.a({negative, result}), .b({8{1'b0}}), .eq(NewAluFlags[2]));  // open: gt, lt
  Multiplexer #(.Selector_Bits(2)) multiplexer_11 (
    .sel(AdderSelect), .in_0(1'b0), .in_1(1'b1), .in_2(AluFlags[3]), .in_3(1'b0), .out(multiplexer_11_out));
  Multiplexer #(.Selector_Bits(2), .Bits(8)) multiplexer_12 (
    .sel(OffsetMode), .in_0({8{1'b0}}), .in_1(off), .in_2(8'h1), .in_3({8{1'b1}}), .out(multiplexer_12_out));
  Register #(.Bits(4)) Bank_Register (.D(DataBus[3:0]), .C(clk), .en(LoadBR), .Q(br));
  or or_4 (or_4_out, and_4_out, Flags[2]);
  // Probe on {negative, result}
  // Probe on {left_sign, shift}
  // Probe on \logic 
  BitExtender bitextender_1 (.in(multiplexer_12_out), .out(bitextender_1_out));
  Multiplexer #(.Bits(8)) multiplexer_13 (
    .sel(ResultSelect), .in_0({AluFlags, Flags}), .in_1({negative, result}), .out(multiplexer_13_out));
  Multiplexer #(.Selector_Bits(3)) multiplexer_14 (
    .sel({negative, left_sign, \logic [7]}), .in_0(1'b0), .in_1(1'b0), .in_2(1'b0), .in_3(1'b1), .in_4(1'b1),
    .in_5(1'b0), .in_6(1'b0), .in_7(1'b0), .out(NewAluFlags[1]));
  // Probe on br
  // Probe on off
  Add #(.Bits(16)) add_2 (.a(bitextender_1_out), .b(multiplexer_8_out), .c_i(1'b0), .s(add_2_s));  // open: c_o
  Multiplexer #(.Bits(4)) multiplexer_15 (.sel(or_4_out), .in_0(4'b0000), .in_1(br), .out(multiplexer_15_out));
  Multiplexer #(.Bits(8)) multiplexer_16 (
    .sel(RegisterWriteBackSelect), .in_0(multiplexer_13_out), .in_1(mdi), .out(DataBus));
  D_FF #(.Bits(8)) Data_Register__Out (.D(multiplexer_13_out), .C(clk), .Q(mdo));  // open: nQ
  Multiplexer #(.Selector_Bits(2)) multiplexer_17 (
    .sel(IrqEnableFlagControl), .in_0(Flags[0]), .in_1(Flags[0]), .in_2(1'b0), .in_3(1'b1), .out(NewIrqEnable));
  Multiplexer #(.Selector_Bits(2)) multiplexer_18 (
    .sel(UserDataFlagControl), .in_0(Flags[1]), .in_1(Flags[1]), .in_2(1'b0), .in_3(1'b1), .out(NewUserData));
  // Probe on mcr
  // Probe on mbr
  // Probe on mar
  D_FF #(.Bits(16)) Addr_Register (.D(add_2_s), .C(clk), .Q(mar));  // open: nQ
  D_FF #(.Bits(4)) Bank_Register_2 (.D(multiplexer_15_out), .C(clk), .Q(mbr));  // open: nQ
  D_FF #(.Bits(3)) Control_Register (.D({nCodeAccess, nIOAccess, Flags[2]}), .C(clk), .Q(mcr));  // open: nQ
  D_FF #(.Bits(8)) Data_Register__In (.D(MemoryData), .C(clk), .Q(mdi));  // open: nQ
  assign Address = AssertSystemBus ? mar : 16'bz;  // Driver driver_1
  assign Bank = AssertSystemBus ? mbr : 4'bz;  // Driver driver_2
  assign Control = AssertSystemBus ? mcr : 3'bz;  // Driver driver_3
  assign MemoryData = Write ? mdo : 8'bz;  // Driver driver_4
  and and_5 (and_5_out, ~Flags[2], LoadFlags);  // And
  ROM #(.AddrBits(16), .Bits(8)) rom_1 (.A(Address), .sel(1'b1), .D(MemoryData));
  Multiplexer #(.Bits(4)) multiplexer_19 (
    .sel(and_5_out), .in_0({NewNmiActive, NewnKernel, NewUserData, NewIrqEnable}), .in_1(DataBus[3:0]),
    .out(multiplexer_19_out));
  Multiplexer #(.Bits(4)) multiplexer_20 (
    .sel(and_5_out), .in_0({carry, NewAluFlags, negative}), .in_1(DataBus[7:4]), .out(multiplexer_20_out));
  and and_6 (NewnKernel, ~EnterKernelMode, Flags[2]);  // And
  or or_5 (NewNmiActive, SetNmiActive, Flags[3]);
  Register #(.Bits(4)) SysFlags (.D(multiplexer_19_out), .C(clk), .en(1'b1), .Q(Flags));
  Register #(.Bits(4)) u_AluFlags (.D(multiplexer_20_out), .C(clk), .en(1'b1), .Q(AluFlags));
  LED IrqEnable (.in(Flags[0]));
  LED UserData (.in(Flags[1]));
  LED nKernel (.in(Flags[2]));
  LED NmiActive (.in(Flags[3]));
  LED Sign (.in(AluFlags[0]));
  LED Overflow (.in(AluFlags[1]));
  LED Zero (.in(AluFlags[2]));
  LED u_Carry (.in(AluFlags[3]));

  // Other names for the same wires on the sheet: Flags[7:4] = AluFlags; SignFlag = AluFlags[0];
  //   OverflowFlag = AluFlags[1]; ZeroFlag = AluFlags[2]; CarryFlag = AluFlags[3];
  //   NewAluFlags (some bits) = {carry, negative}; right_sign = \logic [7]; overflow = NewAluFlags[1];
  //   result[7] = negative; shift[7] = left_sign; IrqEnable = Flags[0]; SysFlags[3:0] = Flags; UserData = Flags[1];
  //   nKernel = Flags[2]; NmiActive = Flags[3]; zero = NewAluFlags[2]

  // Notes on the sheet:
  //   Control Unit
  //   TODO: Reset Logic
  //   Reset Logic
  //   - Asynchronous Activation?
  //   - Synchronous Deactivation?
  //   - Reset via IO?
  //   - Reset upon nested NMI.
  //   TODO: Generate ACK Signal.
  //   Just ~AssertSystemBus?
  //   Other reset considerations
  //   - Clear program counter
  //   - Clear control latches (JK Flip Flops?)
  //   - Clear extension bit
  //   - Clear interrupt latch
  //   Mem/~IO  ^^^
  //   <<< NoClockPointerSelect
  //   A Register
  //   B Register
  //   C Register
  //   D Register
  //   Logic
  //   Shift
  //   Result
  //   FlagControl
  //   1 - ChangeFlag
  //   0 - NewValue
  //   Temp Register
  //   TODO: Encode SysFlags control lines
  //   Program Counter
  //   Stack Pointer
  //   X Pointer
  //   Y Pointer
  //   Temp Pointer
  //   Bank Register
  //   Addr Register
  //   MDR_out
  //   MDR_in
  //   ResetSequencer
  //   Pointer File
  //   Interrupt Vectors
  //   Register File
  //   Arithmetic & Logic Unit
  //   Address Generation Unit
  //   .
  //   contents of Logic_Unit (hex, n*v repeats v):
  //   5
  //   bw8 cpu rev2
  //   ***july 2023***
  //   8-bit WriteBack
  //   Status Flags
  //   Offset Register
  //   16-bit WriteBack
  //   Control Register
  //   Only allow writes to Flags
  //   while in KernelMode
  //   Memory & IO
  //   contents of rom_1 (hex, n*v repeats v):
  //   5
endmodule
